// Logisim project ETFStudent.circ as structural Verilog: 3 circuits, main circuit KMADR
module KMADR (
  input  immed,
  input  memdir,
  input  memind,
  input  regind,
  input  postincr,
  input  postdec,
  input  regdir,
  output [4:0] Adr
);

  assign Adr = immed ? 5'b00010 : 5'bz;  // Controlled_Buffer controlled_buffer_1
  assign Adr = memdir ? 5'b00011 : 5'bz;  // Controlled_Buffer controlled_buffer_2
  assign Adr = memind ? 5'b00100 : 5'bz;  // Controlled_Buffer controlled_buffer_3
  assign Adr = regind ? 5'b01001 : 5'bz;  // Controlled_Buffer controlled_buffer_4
  assign Adr = postincr ? 5'b01010 : 5'bz;  // Controlled_Buffer controlled_buffer_5
  assign Adr = postdec ? 5'b01011 : 5'bz;  // Controlled_Buffer controlled_buffer_6
  assign Adr = regdir ? 5'b10001 : 5'bz;  // Controlled_Buffer controlled_buffer_7
endmodule

module KMOPR (
  input  HALT,
  input  RTS,
  input  RTI,
  input  ROTR,
  input  ROTRC,
  input  PUSH,
  input  POP,
  input  BLEQ,
  input  BGREU,
  input  BNNG,
  input  BGRT,
  input  JLEQ,
  input  JSR,
  input  JMP,
  input  LD,
  input  ST,
  input  ADD,
  input  INC,
  input  LOR,
  input  STRFIND,
  output [6:0] Adr
);

  assign Adr = HALT ? 7'b0000010 : 7'bz;  // Controlled_Buffer controlled_buffer_1
  assign Adr = RTS ? 7'b0000011 : 7'bz;  // Controlled_Buffer controlled_buffer_2
  assign Adr = RTI ? 7'b0001001 : 7'bz;  // Controlled_Buffer controlled_buffer_3
  assign Adr = ROTR ? 7'b0011000 : 7'bz;  // Controlled_Buffer controlled_buffer_4
  assign Adr = ROTRC ? 7'b0011001 : 7'bz;  // Controlled_Buffer controlled_buffer_5
  assign Adr = PUSH ? 7'b0011010 : 7'bz;  // Controlled_Buffer controlled_buffer_6
  assign Adr = POP ? 7'b0100000 : 7'bz;  // Controlled_Buffer controlled_buffer_7
  assign Adr = BLEQ ? 7'b0101000 : 7'bz;  // Controlled_Buffer controlled_buffer_8
  assign Adr = BGREU ? 7'b0101010 : 7'bz;  // Controlled_Buffer controlled_buffer_9
  assign Adr = BNNG ? 7'b0101100 : 7'bz;  // Controlled_Buffer controlled_buffer_10
  assign Adr = BGRT ? 7'b0101110 : 7'bz;  // Controlled_Buffer controlled_buffer_11
  assign Adr = JLEQ ? 7'b0110000 : 7'bz;  // Controlled_Buffer controlled_buffer_12
  assign Adr = JSR ? 7'b0110011 : 7'bz;  // Controlled_Buffer controlled_buffer_13
  assign Adr = JMP ? 7'b0110010 : 7'bz;  // Controlled_Buffer controlled_buffer_14
  assign Adr = LD ? 7'b0111010 : 7'bz;  // Controlled_Buffer controlled_buffer_15
  assign Adr = ST ? 7'b1100010 : 7'bz;  // Controlled_Buffer controlled_buffer_16
  assign Adr = ADD ? 7'b0111100 : 7'bz;  // Controlled_Buffer controlled_buffer_17
  assign Adr = INC ? 7'b1100010 : 7'bz;  // Controlled_Buffer controlled_buffer_18
  assign Adr = LOR ? 7'b0111110 : 7'bz;  // Controlled_Buffer controlled_buffer_19
  assign Adr = STRFIND ? 7'b1100010 : 7'bz;  // Controlled_Buffer controlled_buffer_20
endmodule

module GPR16x16 (
  input  [15:0] DI,
  input  [3:0] A,
  input  WR,
  input  CLK,
  input  rst,
  output [15:0] DO
);

  wire and_1_out, and_2_out, and_3_out, and_4_out, and_5_out, and_6_out, and_7_out, and_8_out, and_9_out,
       and_10_out, and_11_out, and_12_out, and_13_out, and_14_out, and_15_out, and_16_out, CS0, CS1, CS2,
       CS3, CS4, CS5, CS6, CS7, CS8, CS9, CS10, CS11, CS12, CS13, CS14, CS15;
  wire [15:0] register_1_q, register_2_q, register_3_q, register_4_q, register_5_q, register_6_q,
       register_7_q, register_8_q, register_9_q, register_10_q, register_11_q, register_12_q, register_13_q,
       register_14_q, register_15_q, register_16_q;

  Decoder #(.enable("false"), .select(4)) decoder_1 (
    .out0(CS0), .out1(CS1), .out2(CS2), .out3(CS3), .out4(CS4), .out5(CS5), .out6(CS6), .out7(CS7),
    .out8(CS8), .out9(CS9), .out10(CS10), .out11(CS11), .out12(CS12), .out13(CS13), .out14(CS14),
    .out15(CS15), .sel(A));
  and and_1 (and_1_out, CS0, WR);
  and and_2 (and_2_out, CS1, WR);
  and and_3 (and_3_out, CS2, WR);
  and and_4 (and_4_out, CS3, WR);
  Register #(.width(16)) register_1 (.D(DI), .en(and_1_out), .clk(CLK), .Q(register_1_q), .clr(rst));
  Register #(.width(16)) register_2 (.D(DI), .en(and_2_out), .clk(CLK), .Q(register_2_q), .clr(rst));
  Register #(.width(16)) register_3 (.D(DI), .en(and_3_out), .clk(CLK), .Q(register_3_q), .clr(rst));
  Register #(.width(16)) register_4 (.D(DI), .en(and_4_out), .clk(CLK), .Q(register_4_q), .clr(rst));
  assign DO = CS0 ? register_1_q : 16'bz;  // Controlled_Buffer controlled_buffer_1
  assign DO = CS1 ? register_2_q : 16'bz;  // Controlled_Buffer controlled_buffer_2
  assign DO = CS2 ? register_3_q : 16'bz;  // Controlled_Buffer controlled_buffer_3
  assign DO = CS3 ? register_4_q : 16'bz;  // Controlled_Buffer controlled_buffer_4
  Register #(.width(16)) register_5 (.D(DI), .en(and_5_out), .clk(CLK), .Q(register_5_q), .clr(rst));
  and and_5 (and_5_out, CS4, WR);
  Register #(.width(16)) register_6 (.D(DI), .en(and_6_out), .clk(CLK), .Q(register_6_q), .clr(rst));
  and and_6 (and_6_out, CS5, WR);
  Register #(.width(16)) register_7 (.D(DI), .en(and_7_out), .clk(CLK), .Q(register_7_q), .clr(rst));
  and and_7 (and_7_out, CS6, WR);
  Register #(.width(16)) register_8 (.D(DI), .en(and_8_out), .clk(CLK), .Q(register_8_q), .clr(rst));
  and and_8 (and_8_out, CS7, WR);
  assign DO = CS4 ? register_5_q : 16'bz;  // Controlled_Buffer controlled_buffer_5
  assign DO = CS5 ? register_6_q : 16'bz;  // Controlled_Buffer controlled_buffer_6
  assign DO = CS6 ? register_7_q : 16'bz;  // Controlled_Buffer controlled_buffer_7
  assign DO = CS7 ? register_8_q : 16'bz;  // Controlled_Buffer controlled_buffer_8
  Register #(.width(16)) register_9 (.D(DI), .en(and_9_out), .clk(CLK), .Q(register_9_q), .clr(rst));
  and and_9 (and_9_out, CS8, WR);
  Register #(.width(16)) register_10 (.D(DI), .en(and_10_out), .clk(CLK), .Q(register_10_q), .clr(rst));
  and and_10 (and_10_out, CS9, WR);
  Register #(.width(16)) register_11 (.D(DI), .en(and_11_out), .clk(CLK), .Q(register_11_q), .clr(rst));
  and and_11 (and_11_out, CS10, WR);
  Register #(.width(16)) register_12 (.D(DI), .en(and_12_out), .clk(CLK), .Q(register_12_q), .clr(rst));
  and and_12 (and_12_out, CS11, WR);
  assign DO = CS8 ? register_9_q : 16'bz;  // Controlled_Buffer controlled_buffer_9
  assign DO = CS9 ? register_10_q : 16'bz;  // Controlled_Buffer controlled_buffer_10
  assign DO = CS10 ? register_11_q : 16'bz;  // Controlled_Buffer controlled_buffer_11
  assign DO = CS11 ? register_12_q : 16'bz;  // Controlled_Buffer controlled_buffer_12
  and and_13 (and_13_out, CS12, WR);
  and and_14 (and_14_out, CS13, WR);
  and and_15 (and_15_out, CS14, WR);
  and and_16 (and_16_out, CS15, WR);
  Register #(.width(16)) register_13 (.D(DI), .en(and_13_out), .clk(CLK), .Q(register_13_q), .clr(rst));
  Register #(.width(16)) register_14 (.D(DI), .en(and_14_out), .clk(CLK), .Q(register_14_q), .clr(rst));
  Register #(.width(16)) register_15 (.D(DI), .en(and_15_out), .clk(CLK), .Q(register_15_q), .clr(rst));
  Register #(.width(16)) register_16 (.D(DI), .en(and_16_out), .clk(CLK), .Q(register_16_q), .clr(rst));
  assign DO = CS12 ? register_13_q : 16'bz;  // Controlled_Buffer controlled_buffer_13
  assign DO = CS13 ? register_14_q : 16'bz;  // Controlled_Buffer controlled_buffer_14
  assign DO = CS14 ? register_15_q : 16'bz;  // Controlled_Buffer controlled_buffer_15
  assign DO = CS15 ? register_16_q : 16'bz;  // Controlled_Buffer controlled_buffer_16

  // Other names for the same wires on the sheet: inREG[15:0] = DI; outREG[15:0] = DO
endmodule
