// Logisim project ORT2Project.circ as structural Verilog: 8 circuits, main circuit CPU
module COMPUTER (
);

  wire BTN_INTR0_out, BTN_INTR1_out, BTN_INTR2_out, BTN_INTR3_out, BTN_RST_out, CLK, cpu_1_p10,
       pull_resistor_4_node, pull_resistor_5_node, ram_1_out_8, rst;
  wire [1:0] cpu_1_p11;
  wire [3:0] cpu_1_p9;
  wire [7:0] pull_resistor_3_node, ram_1_out_7;
  wire [15:0] pull_resistor_1_node;

  Button BTN_RST (.out(BTN_RST_out));
  Clock u_CLK (.out(CLK));
  RisingEdge risingedge_1 (.OUTPUT(rst), .CLK(CLK), .INPUT(BTN_RST_out));
  RAM ram_1 (
    .out_8(ram_1_out_8), .out_7(ram_1_out_7), .in_2(CLK), .in_3(pull_resistor_3_node),
    .in_4(pull_resistor_4_node), .in_5(pull_resistor_5_node), .in_6(rst), .in_1(pull_resistor_1_node));
  Pull_Resistor pull_resistor_1 (.node(pull_resistor_1_node));
  Pull_Resistor pull_resistor_2 (.node(ram_1_out_7));
  Pull_Resistor pull_resistor_3 (.node(pull_resistor_3_node));
  Pull_Resistor pull_resistor_4 (.node(pull_resistor_4_node));
  Pull_Resistor pull_resistor_5 (.node(pull_resistor_5_node));
  Pull_Resistor pull_resistor_6 (.node(ram_1_out_8));
  // CPU cpu_1: pin names not known; wires that end beside it: pull_resistor_1_node, pull_resistor_3_node, ram_1_out_7, pull_resistor_4_node, pull_resistor_5_node, ram_1_out_8, rst, CLK, cpu_1_p9, cpu_1_p10, cpu_1_p11
  INTERRUPT_INTERFACE_4 interrupt_interface_4_1 (
    .intr(cpu_1_p9), .BTN_INTR0(BTN_INTR0_out), .BTN_INTR1(BTN_INTR1_out), .BTN_INTR2(BTN_INTR2_out),
    .BTN_INTR3(BTN_INTR3_out), .inta(cpu_1_p10), .UEXT(cpu_1_p11), .CLK(CLK));
  Button BTN_INTR3 (.out(BTN_INTR3_out));
  Button BTN_INTR2 (.out(BTN_INTR2_out));
  Button BTN_INTR1 (.out(BTN_INTR1_out));
  Button BTN_INTR0 (.out(BTN_INTR0_out));
endmodule

module CPU (
  input  in_1,
  input  in_2,
  input  in_3,
  input  [7:0] DIN,
  input  [3:0] intr3_0,
  output [15:0] ABUS,
  output [7:0] DOUTBUS,
  output out_8,
  output out_9,
  output inta,
  output [1:0] UEXT
);

  wire [3:0] common_1_phaseffbus;
  wire [5:0] pull_resistor_1_node;
  wire [7:0] common_1_addrbus, pull_resistor_6_node;
  wire [8:0] pull_resistor_7_node;
  wire [15:0] A, ALU, B, INTRADDR, PSW, pull_resistor_5_node;
  wire [20:0] common_1_instrucbus;

  COMMON common_1 (
    .MAR(ABUS), .MDR(DOUTBUS), .PHASEFFBUS(common_1_phaseffbus), .ADDRBUS(common_1_addrbus), .PSW(PSW),
    .B(B), .INSTRUCBUS(common_1_instrucbus), .DIN(DIN), .IVTPPDSP(INTRADDR), .CLK(in_2), .RST(in_1),
    .CMEMBUS(pull_resistor_5_node), .CREGBUS(pull_resistor_7_node), .CPSW(pull_resistor_1_node),
    .CFFBUS(pull_resistor_6_node), .A(A), .ALU(ALU));
  Pull_Resistor pull_resistor_1 (.node(pull_resistor_1_node));
  Pull_Resistor pull_resistor_2 (.node(common_1_phaseffbus));
  Pull_Resistor pull_resistor_3 (.node(common_1_instrucbus));
  Pull_Resistor pull_resistor_4 (.node(common_1_addrbus));
  Pull_Resistor pull_resistor_5 (.node(pull_resistor_5_node));
  Pull_Resistor pull_resistor_6 (.node(pull_resistor_6_node));
  Pull_Resistor pull_resistor_7 (.node(pull_resistor_7_node));
  FETCH fetch_1 (
    .CMEMBUS(pull_resistor_5_node), .CFFBUS(pull_resistor_6_node), .CREGBUS(pull_resistor_7_node),
    .rdMEM(out_9), .in_1(in_1), .in_2(in_2), .in_3(in_3), .PSW(PSW), .PHASEFFBUS(common_1_phaseffbus),
    .ADDRBUS(common_1_addrbus), .INSTRUCBUS(common_1_instrucbus));
  ADDR addr_1 (
    .rdMEM(out_9), .in_1(in_1), .in_2(in_2), .in_3(in_3));  // open: CMEMBUS, CFFBUS, CREGBUS, out_10, PHASEFFBUS, ADDRBUS, INSTRUCBUS
  EXEC exec_1 ();  // open: CPSW, CREGBUS, CMEMBUS, CFFBUS, A, ALU, rdMEM, wrMEM, PSW, in_1, in_2, in_3, B, ADDRBUS, PHASEFFBUS, INSTRUCBUS
  INTR intr_1 ();  // open: UEXT, inta, CMEMBUS, ADDIVTP, CREGBUS, CFFBUS, rdMEM, wrMEM, in_7, in_1, in_2, in_3, PSW, PHASEFFBUS, INSTRUCBUS

  // Other names for the same wires on the sheet: CLK = in_2; FCBUS = in_3; MAR[15:0] = ABUS; MDR[7:0] = DOUTBUS;
  //   RD = out_9; rst = in_1; WR = out_8
endmodule

module COMMON (
  input  CLK,
  input  RST,
  input  [7:0] DIN,
  input  [15:0] A,
  input  [15:0] IVTPPDSP,
  input  [15:0] ALU,
  input  [15:0] CMEMBUS,
  input  [7:0] CFFBUS,
  input  [8:0] CREGBUS,
  input  [5:0] CPSW,
  output [15:0] MAR,
  output [20:0] INSTRUCBUS,
  output [7:0] MDR,
  output [3:0] PHASEFFBUS,
  output [7:0] ADDRBUS,
  output [15:0] PSW,
  output [15:0] B
);

  wire adr, bezadr, branch3, decoder_2_out5, decoder_2_out6, decoder_2_out7, decoder_3_out6, decoder_3_out7,
       decoder_5_out7, invalid_group, invalid_instr1, invalid_instr2, invalid_instr3, invalid_instr4, jmp3,
       mxGPRADDR, not_1_out, or_5_out, or_7_out;
  wire [2:0] instr, multiplexer_3_out;
  wire [7:0] IR7_0, IR15_8, IR23_16;
  wire [7:3] IR31_24;
  wire [15:0] GPR, multiplexer_1_out, multiplexer_2_out, PC, SP;

  Multiplexer #(.enable("false"), .select(3), .width(16)) multiplexer_1 (
    .in0(16'h1000), .in1(PC), .in2({IR15_8, IR7_0}), .in3({MDR, {8{1'b0}}}), .in4(GPR),
    .out(multiplexer_1_out), .sel(CMEMBUS[9:7]));  // open: in5, in6, in7
  REG16_INC_LD reg16_inc_ld_1 (
    .A(MAR), .INC(CMEMBUS[1]), .CLK(CLK), .I(multiplexer_1_out), .LD(CMEMBUS[0]));  // open: mr
  Register register_1 (.D(MDR), .en(CREGBUS[3]), .clk(CLK), .Q({IR31_24, instr}));  // open: clr
  Register register_2 (.D(MDR), .en(CREGBUS[1]), .clk(CLK), .Q(IR15_8));  // open: clr
  or or_1 (invalid_group, IR31_24[6], IR31_24[3], IR31_24[7]);
  Decoder #(.enable("false"), .select(2)) decoder_1 (
    .out0(bezadr), .out1(branch3), .out2(jmp3), .out3(adr), .sel(IR31_24[5:4]));
  Decoder #(.select(3)) decoder_2 (
    .out0(INSTRUCBUS[7]), .out1(INSTRUCBUS[8]), .out2(INSTRUCBUS[9]), .out3(INSTRUCBUS[10]),
    .out4(INSTRUCBUS[11]), .out5(decoder_2_out5), .out6(decoder_2_out6), .out7(decoder_2_out7), .sel(instr),
    .en(branch3));
  Decoder #(.select(3)) decoder_3 (
    .out0(INSTRUCBUS[14]), .out1(INSTRUCBUS[15]), .out2(INSTRUCBUS[16]), .out3(INSTRUCBUS[17]),
    .out4(INSTRUCBUS[18]), .out5(INSTRUCBUS[19]), .out6(decoder_3_out6), .out7(decoder_3_out7), .sel(instr),
    .en(adr));
  or or_2 (invalid_instr1, decoder_2_out7, decoder_2_out6, decoder_2_out5);
  or or_3 (invalid_instr3, decoder_3_out7, decoder_3_out6);
  or or_4 (INSTRUCBUS[20], invalid_group, invalid_instr1, invalid_instr2, invalid_instr3, invalid_instr4);
  Register register_3 (.D(DIN), .en(CMEMBUS[2]), .clk(CLK), .Q(MDR));  // open: clr
  Register register_4 (.D(MDR), .en(CREGBUS[2]), .clk(CLK), .Q(IR23_16));  // open: clr
  Register register_5 (.D(MDR), .en(CREGBUS[0]), .clk(CLK), .Q(IR7_0));  // open: clr
  Decoder #(.select(3)) decoder_4 (
    .out0(INSTRUCBUS[0]), .out1(INSTRUCBUS[1]), .out2(INSTRUCBUS[2]), .out3(INSTRUCBUS[3]),
    .out4(INSTRUCBUS[4]), .out5(INSTRUCBUS[5]), .out6(INSTRUCBUS[6]), .out7(invalid_instr4), .sel(instr),
    .en(bezadr));
  or or_5 (or_5_out, instr[2], instr[1]);
  Decoder #(.select(3)) decoder_5 (
    .out0(ADDRBUS[0]), .out1(ADDRBUS[1]), .out2(ADDRBUS[2]), .out3(ADDRBUS[3]), .out4(ADDRBUS[4]),
    .out5(ADDRBUS[5]), .out6(ADDRBUS[6]), .out7(decoder_5_out7), .sel(IR23_16[2:0]), .en(adr));
  not not_1 (not_1_out, instr[0]);
  or or_6 (ADDRBUS[7], IR23_16[3], decoder_5_out7);
  and and_1 (INSTRUCBUS[12], instr[0], jmp3);
  and and_2 (INSTRUCBUS[13], not_1_out, jmp3);
  and and_3 (invalid_instr2, jmp3, or_5_out);
  S_R_Flip_Flop s_r_ff_1 (.S(CFFBUS[0]), .R(CFFBUS[1]), .clk(CLK), .Q(PHASEFFBUS[0]), .preset(RST));  // open: reset, Qn
  Multiplexer #(.enable("false"), .select(2), .width(16)) multiplexer_2 (
    .in0(16'h1000), .in1({{8{1'b0}}, MDR}), .in2({MDR, PC[7:0]}), .out(multiplexer_2_out), .sel(CMEMBUS[6:5]));  // open: in3
  REG16_INC_LD reg16_inc_ld_2 (.A(PC), .INC(CMEMBUS[4]), .CLK(CLK), .I(multiplexer_2_out), .LD(or_7_out));  // open: mr
  or or_7 (or_7_out, CMEMBUS[3], RST);
  S_R_Flip_Flop s_r_ff_2 (.S(CFFBUS[2]), .R(CFFBUS[3]), .clk(CLK), .Q(PHASEFFBUS[1]), .reset(RST));  // open: Qn, preset
  S_R_Flip_Flop s_r_ff_3 (.S(CFFBUS[4]), .R(CFFBUS[5]), .clk(CLK), .Q(PHASEFFBUS[2]), .reset(RST));  // open: Qn, preset
  REG16 reg16_1 (
    .I(SP), .A(16'hf000), .DEC(CMEMBUS[15]), .INC(CMEMBUS[14]), .CLK(CLK), .LD(RST));  // open: Cout, Eout, SL, IL, mr, SR, IR, CL
  S_R_Flip_Flop s_r_ff_4 (.R(CPSW[0]), .clk(CLK), .Q(PSW[0]), .preset(RST));  // open: S, reset, Qn
  S_R_Flip_Flop s_r_ff_5 (.clk(CLK), .Q(PSW[1]), .reset(RST));  // open: S, R, Qn, preset
  S_R_Flip_Flop s_r_ff_6 (.clk(CLK), .Q(PSW[2]), .reset(RST));  // open: S, R, Qn, preset
  S_R_Flip_Flop s_r_ff_7 (.clk(CLK), .Q(PSW[3]), .reset(RST));  // open: S, R, Qn, preset
  S_R_Flip_Flop s_r_ff_8 (.clk(CLK), .Q(PSW[4]), .reset(RST));  // open: S, R, Qn, preset
  S_R_Flip_Flop s_r_ff_9 (.clk(CLK), .Q(PSW[15]), .preset(RST));  // open: S, R, reset, Qn
  Multiplexer #(.enable("false"), .width(3)) multiplexer_3 (
    .in0(IR23_16[2:0]), .out(multiplexer_3_out), .sel(mxGPRADDR));  // open: in1
  S_R_Flip_Flop s_r_ff_10 (
    .S(CFFBUS[6]), .R(CFFBUS[7]), .clk(CLK), .Q(PHASEFFBUS[3]), .reset(RST));  // open: Qn, preset
  Multiplexer #(.enable("false"), .width(16)) multiplexer_4 (.sel(CMEMBUS[11]));  // open: in0, in1, out
  GPR8x16 gpr8x16_1 (.DO(GPR), .CLK(CLK), .A(multiplexer_3_out));  // open: WR, DI
  Multiplexer #(.enable("false"), .select(2), .width(16)) multiplexer_5 (
    .in0({IR15_8, IR7_0}), .in1({MDR, {8{1'b0}}}), .in2({B[15:8], MDR}), .sel(CMEMBUS[13:12]));  // open: in3, out

  // Other names for the same wires on the sheet: mxMAR0 = CMEMBUS[7]; mxMAR1 = CMEMBUS[8]; mxMAR2 = CMEMBUS[9];
  //   mxPC0 = CMEMBUS[5]; mxPC1 = CMEMBUS[6]; mxB0 = CMEMBUS[12]; mxB1 = CMEMBUS[13]; immed = ADDRBUS[0];
  //   memdir = ADDRBUS[1]; memind = ADDRBUS[2]; regind = ADDRBUS[3]; postincr = ADDRBUS[4]; postdec = ADDRBUS[5];
  //   regdir = ADDRBUS[6]; graddr = ADDRBUS[7]; stFETCH = CFFBUS[0]; clFETCH = CFFBUS[1]; stADDR = CFFBUS[2];
  //   clADDR = CFFBUS[3]; stEXEC = CFFBUS[4]; clEXEC = CFFBUS[5]; stINTR = CFFBUS[6]; clINTR = CFFBUS[7];
  //   ldMAR = CMEMBUS[0]; incMAR = CMEMBUS[1]; ldMDR = CMEMBUS[2]; ldPC = CMEMBUS[3]; incPC = CMEMBUS[4];
  //   mxGPRADR = CMEMBUS[10]; mxGPRIN = CMEMBUS[11]; incSP = CMEMBUS[14]; decSP = CMEMBUS[15]; clPSWSTART = CPSW[0];
  //   ldIR7_0 = CREGBUS[0]; ldIR15_8 = CREGBUS[1]; ldIR23_16 = CREGBUS[2]; ldIR31_24 = CREGBUS[3]; wrGPR = CREGBUS[8];
  //   ENTRADDR[15:0] = IVTPPDSP; HALT = INSTRUCBUS[0]; RTS = INSTRUCBUS[1]; RTI = INSTRUCBUS[2]; ROTR = INSTRUCBUS[3];
  //   ROTRC = INSTRUCBUS[4]; PUSH = INSTRUCBUS[5]; POP = INSTRUCBUS[6]; BLEQ = INSTRUCBUS[7]; BGREU = INSTRUCBUS[8];
  //   BNNG = INSTRUCBUS[9]; BGRT = INSTRUCBUS[10]; JLEQ = INSTRUCBUS[11]; JSR = INSTRUCBUS[12]; JMP = INSTRUCBUS[13];
  //   LD = INSTRUCBUS[14]; ST = INSTRUCBUS[15]; ADD = INSTRUCBUS[16]; INC = INSTRUCBUS[17]; LOR = INSTRUCBUS[18];
  //   STRFIND = INSTRUCBUS[19]; grinst = INSTRUCBUS[20]; IR31_24[2:0] = instr; FETCH = PHASEFFBUS[0];
  //   ADDR = PHASEFFBUS[1]; EXEC = PHASEFFBUS[2]; INTR = PHASEFFBUS[3]; PSWSTART = PSW[0]; PSWZ = PSW[1];
  //   PSWN = PSW[2]; PSWV = PSW[3]; PSWC = PSW[4]; PSWI = PSW[15]

  // Notes on the sheet:
  //   MAR
  //   Instrukcijski registar
  //   MDR
  //   Dekoderi za prepoznavanje instrukcije na osnovu sadržaja registra IR31..24
  //   PC
  //   FF za pokretanje FETCH, ADDR, EXEC i INTR faze izvršavanja instrukcije
  //   SP
  //   Registarski fajl
  //   Programska statusna reč (PSW)
  //   B
endmodule

module FETCH (
  input  in_1,
  input  in_2,
  input  in_3,
  input  [3:0] PHASEFFBUS,
  input  [7:0] ADDRBUS,
  input  [15:0] PSW,
  input  [20:0] INSTRUCBUS,
  output [15:0] CMEMBUS,
  output [7:0] CFFBUS,
  output [8:0] CREGBUS,
  output rdMEM
);

  wire addr2, and_1_out, and_2_out, and_3_out, and_4_out, and_5_out, and_6_out, and_7_out, and_8_out,
       and_9_out, bezadr, braddr2, brbezadr, brcnd, brgraddr, brgrinst, brjmp2, brjmp3, brnotFCBUS,
       brnotpswSTARTandFETCH, bruncnd, jmp2, jmp3, not_1_out, not_2_out, not_3_out, or_4_out;
  wire [4:0] reg8_1_i;
  wire [7:0] undriven;
  wire [7:5] reg8_1_i_2;
  wire [14:11] rom_1_data;

  ROM #(.addrWidth(5), .dataWidth(20)) rom_1 (
    .addr(reg8_1_i),
    .data({undriven[4:0], rom_1_data, CFFBUS[4], CFFBUS[2:1], CREGBUS[0], CREGBUS[1], CREGBUS[2], CREGBUS[3], CMEMBUS[2], rdMEM, CMEMBUS[0], CMEMBUS[4]}));
  not not_1 (not_1_out, in_1);
  or or_1 (bezadr, INSTRUCBUS[0], INSTRUCBUS[1], INSTRUCBUS[2], INSTRUCBUS[3], INSTRUCBUS[4], INSTRUCBUS[5], INSTRUCBUS[6]);
  or or_2 (jmp2, INSTRUCBUS[7], INSTRUCBUS[8], INSTRUCBUS[9], INSTRUCBUS[10]);
  or or_3 (jmp3, INSTRUCBUS[11], INSTRUCBUS[12], INSTRUCBUS[13]);
  REG8 reg8_1 (
    .I({reg8_1_i_2, reg8_1_i}), .A(undriven), .INC(not_2_out), .mr(not_1_out), .CLK(in_2), .LD(or_4_out));  // open: Cout, Eout, SL, IL, SR, IR, DEC, CL
  // Probe on {reg8_1_i_2, reg8_1_i}
  not not_2 (not_2_out, or_4_out);
  // Probe on undriven[4:0]
  or or_4 (or_4_out, brcnd, bruncnd);
  or or_5 (addr2, ADDRBUS[0], ADDRBUS[1], ADDRBUS[2], ADDRBUS[3]);
  Decoder #(.enable("false"), .select(4)) decoder_1 (
    .out1(bruncnd), .out2(brnotpswSTARTandFETCH), .out3(brnotFCBUS), .out4(brgrinst), .out5(brbezadr),
    .out6(brjmp2), .out7(braddr2), .out8(brjmp3), .sel(rom_1_data));  // open: out0, out9, out10, out11, out12, out13, out14, out15
  // Probe on rom_1_data
  and and_1 (and_1_out, PSW[0], PHASEFFBUS[0]);
  not not_3 (not_3_out, and_1_out);
  and and_2 (and_2_out, INSTRUCBUS[20], brgrinst);
  and and_3 (and_3_out, ADDRBUS[7], brgraddr);
  and and_4 (and_4_out, bezadr, brbezadr);
  and and_5 (and_5_out, jmp2, brjmp2);
  and and_6 (and_6_out, addr2, braddr2);
  and and_7 (and_7_out, jmp3, brjmp3);
  and and_8 (and_8_out, not_3_out, brnotpswSTARTandFETCH);
  and and_9 (and_9_out, ~in_3, brnotFCBUS);  // AND_Gate
  or or_6 (brcnd, and_8_out, and_9_out, and_2_out, and_3_out, and_4_out, and_5_out, and_6_out, and_7_out);

  // Other names for the same wires on the sheet: immed = ADDRBUS[0]; memdir = ADDRBUS[1]; memind = ADDRBUS[2];
  //   regind = ADDRBUS[3]; postincr = ADDRBUS[4]; postdec = ADDRBUS[5]; regdir = ADDRBUS[6]; graddr = ADDRBUS[7];
  //   stFETCH = CFFBUS[0]; clFETCH = CFFBUS[1]; stADDR = CFFBUS[2]; clADDR = CFFBUS[3]; stEXEC = CFFBUS[4];
  //   clEXEC = CFFBUS[5]; stINTR = CFFBUS[6]; clINTR = CFFBUS[7]; CLK = in_2; ldMAR = CMEMBUS[0]; incMAR = CMEMBUS[1];
  //   ldMDR = CMEMBUS[2]; ldPC = CMEMBUS[3]; incPC = CMEMBUS[4]; mxPC0 = CMEMBUS[5]; mxPC1 = CMEMBUS[6];
  //   mxMAR0 = CMEMBUS[7]; mxMAR1 = CMEMBUS[8]; mxMAR2 = CMEMBUS[9]; mxGPRADR = CMEMBUS[10]; mxGPRIN = CMEMBUS[11];
  //   mxB0 = CMEMBUS[12]; mxB1 = CMEMBUS[13]; incSP = CMEMBUS[14]; decSP = CMEMBUS[15]; ldIR7_0 = CREGBUS[0];
  //   ldIR15_8 = CREGBUS[1]; ldIR23_16 = CREGBUS[2]; ldIR31_24 = CREGBUS[3]; wrGPR = CREGBUS[8]; FCBUS = in_3;
  //   HALT = INSTRUCBUS[0]; RTS = INSTRUCBUS[1]; RTI = INSTRUCBUS[2]; ROTR = INSTRUCBUS[3]; ROTRC = INSTRUCBUS[4];
  //   PUSH = INSTRUCBUS[5]; POP = INSTRUCBUS[6]; BLEQ = INSTRUCBUS[7]; BGREU = INSTRUCBUS[8]; BNNG = INSTRUCBUS[9];
  //   BGRT = INSTRUCBUS[10]; JLEQ = INSTRUCBUS[11]; JSR = INSTRUCBUS[12]; JMP = INSTRUCBUS[13]; LD = INSTRUCBUS[14];
  //   ST = INSTRUCBUS[15]; ADD = INSTRUCBUS[16]; INC = INSTRUCBUS[17]; LOR = INSTRUCBUS[18]; STRFIND = INSTRUCBUS[19];
  //   grinst = INSTRUCBUS[20]; FETCH = PHASEFFBUS[0]; ADDR = PHASEFFBUS[1]; EXEC = PHASEFFBUS[2];
  //   INTR = PHASEFFBUS[3]; pswSTART = PSW[0]; rst = in_1

  // Notes on the sheet:
  //   contents of rom_1 (hex, n*v repeats v):
  //   1000 3 1180c 10 2000 92800 3 3980c 93020 3800 8c000 3 6180c 94840 3 7980c 80 b00 d00
  //   Operaciona jedinica
  //   Kontrolna jedinica
endmodule

module ADDR (
  input  in_1,
  input  in_2,
  input  in_3,
  input  [3:0] PHASEFFBUS,
  input  [7:0] ADDRBUS,
  input  [20:0] INSTRUCBUS,
  output [15:0] CMEMBUS,
  output [7:0] CFFBUS,
  output [8:0] CREGBUS,
  output out_10,
  output rdMEM
);

  wire and_1_out, and_2_out, and_3_out, brcnd, brmul, brnotADDR, brnotFCBUS, brST, bruncnd, ldB, mxGPRIN0,
       not_1_out, not_2_out, not_3_out, not_4_out;
  wire [4:0] kmadr_1_adr, reg8_inc_ld_1_a;
  wire [7:0] multiplexer_1_out;
  wire [7:5] reg8_inc_ld_1_a_2;
  wire [20:13] rom_1_data;

  ROM #(.addrWidth(5), .dataWidth(21)) rom_1 (
    .addr(reg8_inc_ld_1_a),
    .data({rom_1_data, CFFBUS[4:3], CMEMBUS[13:12], mxGPRIN0, CREGBUS[8], CMEMBUS[9:8], CMEMBUS[2], out_10, CMEMBUS[7], CMEMBUS[0], ldB}));
  not not_1 (not_1_out, in_1);
  REG8_INC_LD reg8_inc_ld_1 (
    .A({reg8_inc_ld_1_a_2, reg8_inc_ld_1_a}), .INC(not_2_out), .mr(not_1_out), .CLK(in_2),
    .I(multiplexer_1_out), .LD(brcnd));
  not not_2 (not_2_out, brcnd);
  Multiplexer #(.enable("false"), .width(5)) multiplexer_1 (
    .in0(rom_1_data[20:16]), .in1(kmadr_1_adr), .out(multiplexer_1_out[4:0]), .sel(brmul));
  Decoder #(.enable("false"), .select(3)) decoder_1 (
    .out1(bruncnd), .out2(brnotADDR), .out3(brmul), .out4(brST), .out5(brnotFCBUS), .sel(rom_1_data[15:13]));  // open: out0, out6, out7
  KMADR kmadr_1 (
    .Adr(kmadr_1_adr), .memdir(ADDRBUS[1]), .memind(ADDRBUS[2]), .regind(ADDRBUS[3]), .postincr(ADDRBUS[4]),
    .postdec(ADDRBUS[5]), .regdir(ADDRBUS[6]), .immed(ADDRBUS[0]));
  not not_3 (not_3_out, PHASEFFBUS[1]);
  not not_4 (not_4_out, in_3);
  and and_1 (and_1_out, brnotADDR, not_3_out);
  and and_2 (and_2_out, brST, INSTRUCBUS[15]);
  and and_3 (and_3_out, brnotFCBUS, not_4_out);
  or or_1 (brcnd, bruncnd, brmul, and_1_out, and_2_out, and_3_out);

  // Other names for the same wires on the sheet: rdMEM_t = out_10; immed = ADDRBUS[0]; memdir = ADDRBUS[1];
  //   memind = ADDRBUS[2]; regind = ADDRBUS[3]; postincr = ADDRBUS[4]; postdec = ADDRBUS[5]; regdir = ADDRBUS[6];
  //   stFETCH = CFFBUS[0]; clFETCH = CFFBUS[1]; stADDR = CFFBUS[2]; clADDR = CFFBUS[3]; stEXEC = CFFBUS[4];
  //   clEXEC = CFFBUS[5]; stINTR = CFFBUS[6]; clINTR = CFFBUS[7]; CLK = in_2; ldMAR = CMEMBUS[0]; incMAR = CMEMBUS[1];
  //   ldMDR = CMEMBUS[2]; ldPC = CMEMBUS[3]; incPC = CMEMBUS[4]; mxPC0 = CMEMBUS[5]; mxPC1 = CMEMBUS[6];
  //   mxMAR0 = CMEMBUS[7]; mxMAR1 = CMEMBUS[8]; mxMAR2 = CMEMBUS[9]; mxGPRADR = CMEMBUS[10]; mxGPRIN = CMEMBUS[11];
  //   mxB0 = CMEMBUS[12]; mxB1 = CMEMBUS[13]; incSP = CMEMBUS[14]; decSP = CMEMBUS[15]; ldIR7_0 = CREGBUS[0];
  //   ldIR15_8 = CREGBUS[1]; ldIR23_16 = CREGBUS[2]; ldIR31_24 = CREGBUS[3]; wrGPR = CREGBUS[8]; FCBUS = in_3;
  //   HALT = INSTRUCBUS[0]; RTS = INSTRUCBUS[1]; RTI = INSTRUCBUS[2]; ROTR = INSTRUCBUS[3]; ROTRC = INSTRUCBUS[4];
  //   PUSH = INSTRUCBUS[5]; POP = INSTRUCBUS[6]; BLEQ = INSTRUCBUS[7]; BGREU = INSTRUCBUS[8]; BNNG = INSTRUCBUS[9];
  //   BGRT = INSTRUCBUS[10]; JLEQ = INSTRUCBUS[11]; JSR = INSTRUCBUS[12]; JMP = INSTRUCBUS[13]; LD = INSTRUCBUS[14];
  //   ST = INSTRUCBUS[15]; ADD = INSTRUCBUS[16]; INC = INSTRUCBUS[17]; LOR = INSTRUCBUS[18]; STRFIND = INSTRUCBUS[19];
  //   grinst = INSTRUCBUS[20]; ADDR = PHASEFFBUS[1]; rst = in_1

  // Notes on the sheet:
  //   contents of rom_1 (hex, n*v repeats v):
  //   4000 6000 148000 142001 d2006 6 6a018 22 8a018 d2026 d2042 d20c2 1c2 148000 ea018 201 10a018 142401
  //   148000 601 3800
  //   Operaciona jedinica
  //   Upravljačka jedinica
endmodule

module EXEC (
  input  in_1,
  input  in_2,
  input  in_3,
  input  [7:0] B,
  input  [3:0] PHASEFFBUS,
  input  [10:0] INSTRUCBUS,
  input  [3:0] ADDRBUS,
  input  [15:0] PSW,
  output [7:0] A,
  output [7:0] ALU,
  output [14:0] CMEMBUS,
  output [7:0] CFFBUS,
  output [8:0] CREGBUS,
  output [5:0] CPSW,
  output rdMEM,
  output wrMEM
);


  // Other names for the same wires on the sheet: CLK = in_2; FCBUS = in_3; rst = in_1

  // Notes on the sheet:
  //   Operaciona jedinica
  //   Upravljacka jedinica
endmodule

module INTR (
  input  in_1,
  input  in_2,
  input  in_3,
  input  [3:0] PHASEFFBUS,
  input  [10:0] INSTRUCBUS,
  input  [15:0] PSW,
  input  [3:0] in_7,
  output [15:0] ADDIVTP,
  output [1:0] UEXT,
  output inta,
  output [14:0] CMEMBUS,
  output [7:0] CFFBUS,
  output [8:0] CREGBUS,
  output rdMEM,
  output wrMEM
);


  // Other names for the same wires on the sheet: CLK = in_2; FCBUS = in_3; intr[3:0] = in_7; ldBR = inta; rst = in_1

  // Notes on the sheet:
  //   Operaciona jedinica
  //   Upravljacka jedinica
endmodule

module RAM (
  input  [15:0] in_1,
  input  in_2,
  input  [7:0] in_3,
  input  in_4,
  input  in_5,
  input  in_6,
  output [7:0] out_7,
  output out_8
);

  wire and_1_out, and_2_out, CNT0, LDCNT, not_1_out, not_2_out, not_3_out, notCNT0, or_1_out, rsff_2_q, sl,
       xor_1_out;
  wire [3:0] CNT, LFSR;

  RSFF rsff_1 (.Q(sl), .S(in_6), .R(1'b0), .CLK(in_2));  // open: notQ, Sd, Rd
  or or_1 (or_1_out, in_4, in_5);
  REG4_LD_SL_SR reg4_ld_sl_sr_1 (
    .A(LFSR), .IR(1'b0), .SR(1'b0), .IL(xor_1_out), .SL(sl), .CLK(in_2), .I(4'b1111), .LD(in_6));  // open: mr
  RisingEdge risingedge_1 (.OUTPUT(LDCNT), .CLK(in_2), .INPUT(or_1_out));
  MEM64Kx8 mem64kx8_1 (.DOUT(out_7), .CLK(in_2), .A(in_1), .DIN(in_3), .WR_RD(in_4), .CS(1'b1));
  xor xor_1 (xor_1_out, LFSR[2], LFSR[3]);
  and and_1 (and_1_out, CNT0, not_1_out);
  not not_1 (not_1_out, LDCNT);
  RSFF rsff_2 (.Q(rsff_2_q), .Rd(not_2_out), .S(LDCNT), .R(and_1_out), .CLK(in_2));  // open: notQ, Sd
  not not_2 (not_2_out, in_6);
  and and_2 (and_2_out, rsff_2_q, CNT0);
  REG4m_DEC_LD reg4m_dec_ld_1 (
    .A(CNT), .LD(LDCNT), .Ein(notCNT0), .DEC(notCNT0), .CLK(in_2), .I(LFSR));  // open: Eout, mr
  or or_2 (notCNT0, CNT[0], CNT[1], CNT[2], CNT[3]);
  RSFF rsff_3 (.Q(out_8), .Rd(not_3_out), .S(and_2_out), .R(out_8), .CLK(in_2));  // open: notQ, Sd
  not not_3 (not_3_out, in_6);
  not not_4 (CNT0, notCNT0);

  // Other names for the same wires on the sheet: ADR[15:0] = in_1; CLK = in_2; DIN[7:0] = in_3; DOUT[7:0] = out_7;
  //   fc = out_8; RDMEM = in_5; rst = in_6; WRMEM = in_4

  // Notes on the sheet:
  //   Random broj predstavlja vreme pristupa memoriji
  //   Brojac za generisanje random broja 
  //   Jedinica za generisanje function complete (fc) signala
  //   Brojac za dekrementiranje random broja
endmodule
